# Fritzing sketch pullupResistor (saved by Fritzing 0.9.3b)

parts:
  WeMos_D1_Mini1 = WeMos D1 Mini
  S1 = Reed switch [package=THT]
  R1 = Resistor [tolerance=±5% resistance=10k package=THT]

nets:
  N1: WeMos_D1_Mini1.3V3, R1.Pin_0
  N2: WeMos_D1_Mini1.D1, S1.pin_2, R1.Pin_1
  N3: WeMos_D1_Mini1.G, S1.pin_1
